# Fritzing sketch smart-lego (saved by Fritzing 0.9.3b)
breadboards: 1

parts:
  U1 = ATTINY13 [package=dip]
  R1 = Resistor [tolerance=±5% resistance=100 package="1206 [SMD]"]
  LED1 = LED - 5mm [color="White (4500K)" package="5 mm [THT]"]
  3V = Battery Holders [package=battcom_20mm_pth]
  S1 = Momentary Switch [package=ksa_sealed_tac_switch]

nets:
  N1: U1.PB5(NRES), S1.4
  N2: U1.GND, R1.Pin_0, 3V.-, S1.2
  N3: U1.PB0(MOSI), LED1.anode
  N4: U1.VCC, 3V.+
  N5: R1.Pin_1, LED1.cathode
